// Logisim project ControlBateria.circ as structural Verilog: 1 circuit, main circuit main
module main (
  input  Bh,
  input  Bl,
  input  Th,
  output C,
  output A
);

  wire not_1_out, not_2_out;

  not not_1 (not_1_out, Bh);
  and and_1 (C, not_1_out, not_2_out);
  not not_2 (not_2_out, Th);
  or or_1 (A, Bl, Th);
endmodule
